# Fritzing sketch PCB_compactadora (saved by Fritzing 0.9.9b)
circuit board: 15cm x 11cm
breadboards: 1

parts:
  ON/OFF_Switch = SIP - 2 pins [chip_label=cambiar package="SIP (Single Inline) [THT]"]
  Switch_magnetico = SIP - 2 pins [chip_label=cambiar package="SIP (Single Inline) [THT]"]
  Speaker = SIP - 2 pins [chip_label=cambiar package="SIP (Single Inline) [THT]"]
  Red_LED = SIP - 2 pins [chip_label=cambiar package="SIP (Single Inline) [THT]"]
  Green_LED = SIP - 2 pins [chip_label=cambiar package="SIP (Single Inline) [THT]"]
  Compact_button = SIP - 2 pins [chip_label=cambiar package="SIP (Single Inline) [THT]"]
  Lift_Button = SIP - 2 pins [chip_label=cambiar package="SIP (Single Inline) [THT]"]
  Emergency_button = SIP - 2 pins [chip_label=cambiar package="SIP (Single Inline) [THT]"]
  Pantalla_tactil = IC, SIP package, 4 pins [chip_label=NX8048K070]
  V1A = DC Power [voltage=5V]
  RelevadorRLED = IC, DIP package, 6 pins [chip_label=IC]
  RelevadorGLED = IC, DIP package, 6 pins [chip_label=IC]
  RelevadorL = IC, DIP package, 6 pins [chip_label=IC]
  RelevadorR = IC, DIP package, 6 pins [chip_label=IC]
  V4 = DC Power [voltage=24V]
  V3 = DC Power [voltage=12V]
  V2 = DC Power [voltage=12V]
  Electroválvula = IC, SIP package, 3 pins [chip_label=IC]
  V3_2 = DC Power [voltage=24V]
  Arduino_MEGA = Arduino Mega 2560 (Rev3)
  Load_cell = Camdenboss CTB0158-5 [package=THT]
  Load_Amp_1 = IC, SIP package, 5 pins [chip_label=HX711]
  Load_Amp_2 = IC, SIP package, 5 pins

nets:
  N1: ON/OFF_Switch.pin1, Arduino_MEGA.D3_PWM
  GND: ON/OFF_Switch.pin2, Switch_magnetico.pin2, Speaker.pin2, Red_LED.pin2, Green_LED.pin2, Compact_button.pin2, Lift_Button.pin2, Emergency_button.pin2, Pantalla_tactil.pin1, V1A.V-, RelevadorRLED.pin2, RelevadorGLED.pin2, RelevadorL.pin5, RelevadorR.pin5, V3.V-, V2.V-, Electroválvula.pin3, Arduino_MEGA.GND, Load_Amp_1.pin5
  N2: Switch_magnetico.pin1, Arduino_MEGA.D23
  N3: Speaker.pin1, Arduino_MEGA.D9_PWM
  N4: Red_LED.pin1, RelevadorRLED.pin4
  N5: Green_LED.pin1, RelevadorGLED.pin4
  N6: Compact_button.pin1, Arduino_MEGA.D37
  N7: Lift_Button.pin1, Arduino_MEGA.D33
  N8: Emergency_button.pin1, Arduino_MEGA.D35
  N9: Pantalla_tactil.pin2, Arduino_MEGA.D1_TX0
  N10: Pantalla_tactil.pin3, Arduino_MEGA.D0_RX0
  N11: Pantalla_tactil.pin4, V1A.V+
  N12: RelevadorRLED.pin1, RelevadorGLED.pin1, RelevadorL.pin1, RelevadorR.pin1, Arduino_MEGA.5V, Load_Amp_1.pin1, Load_Amp_1.pin2
  N13: RelevadorRLED.pin3, Arduino_MEGA.D46
  N14: RelevadorRLED.pin5, V2.V+
  N15: RelevadorGLED.pin3, Arduino_MEGA.D42
  N16: RelevadorGLED.pin5, V3.V+
  N17: RelevadorL.pin3, Arduino_MEGA.D28
  N18: RelevadorL.pin4, V3_2.V-
  N19: RelevadorR.pin3, Arduino_MEGA.D29
  N20: RelevadorR.pin4, V4.V-
  N21: V4.V+, Electroválvula.pin2
  N22: Electroválvula.pin1, V3_2.V+
  N23: Arduino_MEGA.D4_PWM, Load_Amp_1.pin3
  N24: Arduino_MEGA.D5_PWM, Load_Amp_1.pin4
  N25: Load_cell.pin1, Load_Amp_2.pin1
  N26: Load_cell.pin2, Load_Amp_2.pin2
  N27: Load_cell.pin3, Load_Amp_2.pin3
  N28: Load_cell.pin4, Load_Amp_2.pin4
  N29: Load_cell.pin5, Load_Amp_2.pin5
